# Fritzing sketch lorawan-weather-node-pcb (saved by Fritzing 1.0.7)
circuit board: 10cm x 5cm
breadboards: 1

parts:
  (Heltec_V3) = female pin header, 18 pins [form="♀ (female)"]
  R14 = Resistor [tolerance=±5% power=0.25W resistance=4.7k part_number=MBA02040C4701FRP00 mn=MBA02040C4701FRP00 package=THT]
  C10 = Ceramic Capacitor [capacitance=100nF voltage=50V package="100 mil [THT, multilayer]"]
  Davis_Rain = RJ11 Jack [mn=PRT-00132 package=rj11-6]
  C12 = Ceramic Capacitor [capacitance=1µF voltage=50V package="100 mil [THT, multilayer]"]
  ESP32_LoRa_V3 = female pin header, 18 pins [form="♀ (female)"]
  1w(DS18B20) = female pin header, 3 pins [form="♀ (female)"]
  R11 = Resistor [tolerance=±5% power=0.25W resistance=4.7k part_number=MBA02040C4701FRP00 mn=MBA02040C4701FRP00 package=THT]
  Davis_Wind = RJ11 Jack [part_number=PRT-00132 mn=PRT-00132 package=rj11-6]
  I2C_BME280 = RJ45 Jack [part_number=PRT-00643 mn=PRT-00643 package=rj45-8]
  R4 = Resistor [tolerance=±5% power=0.5W resistance=330 part_number=PR01000103300JA100 mn=PR01000103300JA100 package=THT]
  R7 = Resistor [tolerance=±5% power=0.25W resistance=1k part_number=MBA02040C1001FRP00 mn=MBA02040C1001FRP00 package=THT]
  R9 = Resistor [tolerance=±5% power=0.25W resistance=1k part_number=MBA02040C1001FRP00 mn=MBA02040C1001FRP00 package=THT]
  R8 = Resistor [tolerance=±5% power=0.25W resistance=1k part_number=MBA02040C1001FRP00 mn=MBA02040C1001FRP00 package=THT]
  R6 = Resistor [tolerance=±5% power=0.5W resistance=330 part_number=PR01000103300JA100 mn=PR01000103300JA100 package=THT]
  R13 = Resistor [tolerance=±5% power=0.25W resistance=4.7k part_number=MBA02040C4701FRP00 mn=MBA02040C4701FRP00 package=THT]
  R12 = Resistor [tolerance=±5% power=0.25W resistance=4.7k part_number=MBA02040C4701FRP00 mn=MBA02040C4701FRP00 package=THT]
  R5 = Resistor [tolerance=±5% power=0.5W resistance=330 part_number=PR01000103300JA100 mn=PR01000103300JA100 package=THT]
  R15 = Resistor [tolerance=±5% power=0.25W resistance=4.7k part_number=MBA02040C4701FRP00 mn=MBA02040C4701FRP00 package=THT]
  C9 = Ceramic Capacitor [capacitance=100nF voltage=50V package="100 mil [THT, multilayer]"]
  R3 = Resistor [tolerance=±5% power=0.5W resistance=33 part_number=PR01000103309JA100 mn=PR01000103309JA100 package=THT]
  R2 = Resistor [tolerance=±5% power=0.5W resistance=33 part_number=PR01000103309JA100 mn=PR01000103309JA100 package=THT]
  D5 = Schottky Diode [part_number=BAT43 mn=BAT43 package="300 mil [THT]"]
  D6 = Schottky Diode [part_number=BAT43 mn=BAT43 package="300 mil [THT]"]
  D3 = Schottky Diode [part_number=BAT43 mn=BAT43 package="300 mil [THT]"]
  D4 = Schottky Diode [part_number=BAT43 mn=BAT43 package="300 mil [THT]"]
  R1 = Resistor [tolerance=±5% power=0.5W resistance=33 part_number=PR01000103309JA100 mn=PR01000103309JA100 package=THT]
  C6 = Ceramic Capacitor [capacitance=100nF voltage=50V package="100 mil [THT, multilayer]"]
  D7 = Schottky Diode [part_number=BAT43 mn=BAT43 package="300 mil [THT]"]
  D8 = Schottky Diode [part_number=BAT43 mn=BAT43 package="300 mil [THT]"]
  D10 = Schottky Diode [part_number=BAT43 mn=BAT43 package="300 mil [THT]"]
  D9 = Schottky Diode [part_number=BAT43 mn=BAT43 package="300 mil [THT]"]
  D11 = Schottky Diode [part_number=BAT43 mn=BAT43 package="300 mil [THT]"]
  D12 = Schottky Diode [part_number=BAT43 mn=BAT43 package="300 mil [THT]"]
  F2 = Resettable Fuse PTC [part_number=RXEF017 mn=RXEF017 package=ptc]
  C7 = Ceramic Capacitor [capacitance=100nF voltage=50V package="100 mil [THT, multilayer]"]
  U1 = DIODE-ZENER [part_number=SMLVT3V3 mn=SMLVT3V3 package=smb-diode]
  U6 = DIODE-ZENER [part_number=SMLVT3V3 mn=SMLVT3V3 package=smb-diode]
  U4 = DIODE-ZENER [part_number=SMLVT3V3 mn=SMLVT3V3 package=smb-diode]
  J2 = male pin header, 2 pins [form="♂ (male)"]
  J1 = male pin header, 2 pins [form="♂ (male)"]
  C2 = Capacitor Polarized [package=cpol-radial-100uf-25v]
  U5 = DIODE-ZENER [part_number=SMLVT3V3 mn=SMLVT3V3 package=smb-diode]
  F3 = Resettable Fuse PTC [part_number=RXEF010 mn=RXEF010 package=ptc]
  R10 = Resistor [tolerance=±5% power=0.25W resistance=1k part_number=MBA02040C1001FRP00 mn=MBA02040C1001FRP00 package=THT]
  R20 = Resistor [tolerance=±5% power=0.25W resistance=47k part_number=MBA02040C4702FRP00 mn=MBA02040C4702FRP00 package=THT]
  C8 = Ceramic Capacitor [capacitance=100nF voltage=50V package="100 mil [THT, multilayer]"]
  R18 = Resistor [tolerance=±5% power=0.25W resistance=10k part_number=MBA02040C1002FRP00 mn=MBA02040C1002FRP00 package=THT]
  C3 = Ceramic Capacitor [capacitance=4.7µF voltage=50V mn=FG16X7R1H475KRT06 part_number=FG16X7R1H475KRT06 package="100 mil [THT, multilayer]"]
  C5 = Ceramic Capacitor [capacitance=100nF voltage=50V package="100 mil [THT, multilayer]"]
  U3 = DIODE-ZENER [part_number=SMLVT3V3 mn=SMLVT3V3 package=smb-diode]
  U2 = DIODE-ZENER [part_number=SMLVT3V3 mn=SMLVT3V3 package=smb-diode]
  5V_Input = female pin header, 2 pins [form="♀ (female)"]
  C4 = Ceramic Capacitor [capacitance=100nF voltage=50V package="100 mil [THT, multilayer]"]
  F1 = Resettable Fuse PTC [part_number=RXEF090 mn=RXEF090 package=ptc]
  SMBJ5_0A = DIODE-ZENER [part_number=SMBJ5.0A mn=SMBJ5.0A package=smb-diode]
  D1 = Schottky Diode [part_number=BAT43 mn=BAT43 package="300 mil [THT]"]
  D2 = Schottky Diode [part_number=BAT43 mn=BAT43 package="300 mil [THT]"]
  C11 = Ceramic Capacitor [capacitance=100nF voltage=50V package="100 mil [THT, multilayer]"]
  LP0701N3-G = MOSFET-PCHANNEL LP0701N3-G [mn=LP0701N3-G part_number=LP0701N3-G package=to-92]
  TN2106N3-G = MOSFET-nCHANNEL VN2222L [mn=TN2106N3-G part_number=TN2106N3-G package=to-92]
  D13 = Schottky Diode [part_number=STPS3L60QRL mn=STPS3L60QRL package="300 mil [THT]"]
  C1 = Capacitor Polarized [package=cpol-radial-100uf-25v]
  R21 = Resistor [tolerance=±5% power=0.25W resistance=4.7k part_number=MBA02040C4701FRP00 mn=MBA02040C4701FRP00 package=THT]
  R16 = Resistor [tolerance=±5% power=0.25W resistance=4.7k mn=MBA02040C4701FRP00 part_number=MBA02040C4701FRP00 package=THT]
  R17 = Resistor [tolerance=±5% power=0.25W resistance=10k mn=MBA02040C1002FRP00 part_number=MBA02040C1002FRP00 package=THT]
  R19 = Resistor [tolerance=±5% power=0.25W resistance=10k mn=MBA02040C1002FRP00 part_number=MBA02040C1002FRP00 package=THT]
  SN74LVC2G14DBVR = SN74LVC2G14DBVR [mn=SN74LVC2G14DBVR part_number=SN74LVC2G14DBVR package=SOT23-6]

nets:
  N1: (Heltec_V3).pin1, R9.Pin_0
  N2: (Heltec_V3).pin2, R8.Pin_0
  GPIO 1w: (Heltec_V3).pin3, R11.Pin_1, R1.Pin_1, D1.cathode, D2.anode
  N3: (Heltec_V3).pin6, R7.Pin_0
  GPIO41 i2c SDA: (Heltec_V3).pin11, R2.Pin_1, D3.cathode, D4.anode, J1.pin2
  GPIO42 i2c SCL: (Heltec_V3).pin12, R3.Pin_1, D5.cathode, D6.anode, J2.pin2
  3.3V: (Heltec_V3).pin16, (Heltec_V3).pin17, F2.1
  GND: (Heltec_V3).pin18, C10.1, Davis_Rain.4, C12.1, ESP32_LoRa_V3.pin1, 1w(DS18B20).pin3, Davis_Wind.4, I2C_BME280.1, I2C_BME280.3, I2C_BME280.4, I2C_BME280.6, C9.1, D5.anode, D3.anode, C6.0, D7.anode, D9.anode, D11.anode, C7.0, U1.A, U6.A, U4.A, C2.-, U5.A, C8.0, R18.Pin_1, C3.0, C5.0, U3.A, U2.A, 5V_Input.pin2, C4.0, SMBJ5_0A.A, D1.anode, C11.1, TN2106N3-G.S, D13.anode, C1.-, SN74LVC2G14DBVR.GND
  VCC3.3: R14.Pin_0, Davis_Wind.2, I2C_BME280.7, I2C_BME280.8, R13.Pin_0, R12.Pin_0, R15.Pin_1, C9.0, D6.cathode, D4.cathode, C6.1, D8.cathode, D10.cathode, D12.cathode, F2.2, C7.1, U1.C, U4.C, C2.+, R20.Pin_0, C8.1, D2.cathode, LP0701N3-G.S, R21.Pin_0, SN74LVC2G14DBVR.VCC
  N4: R14.Pin_1, R4.Pin_0, D11.cathode, D12.anode, R16.Pin_1
  GPIO WindSpd: C10.0, R16.Pin_0, SN74LVC2G14DBVR.2A
  N5: Davis_Rain.3, R6.Pin_1, U5.C
  GPIO Rain: C12.0, R17.Pin_0, SN74LVC2G14DBVR.1A
  5V vcc esp32: ESP32_LoRa_V3.pin2, C4.1, F1.2, SMBJ5_0A.C, D13.cathode, C1.+
  GPIO47 HSS: ESP32_LoRa_V3.pin13, R10.Pin_0, R18.Pin_0
  N6: 1w(DS18B20).pin1, R1.Pin_0
  N7: 1w(DS18B20).pin2, R11.Pin_0, U6.C, F3.2, C3.1, C5.1
  N8: Davis_Wind.3, R5.Pin_1, U2.C
  N9: Davis_Wind.5, R4.Pin_1, U3.C
  N10: I2C_BME280.2, R3.Pin_0
  N11: I2C_BME280.5, R2.Pin_0
  ADC WindDir: R7.Pin_1, C11.0, R19.Pin_0
  N12: R9.Pin_1, SN74LVC2G14DBVR.1Y
  N13: R8.Pin_1, SN74LVC2G14DBVR.2Y
  N14: R6.Pin_0, R15.Pin_0, D7.cathode, D8.anode, R17.Pin_1
  N15: R13.Pin_1, J1.pin1
  N16: R12.Pin_1, J2.pin1
  N17: R5.Pin_0, D10.anode, D9.cathode, R21.Pin_1, R19.Pin_1
  N18: F3.1, LP0701N3-G.D
  N19: R10.Pin_1, TN2106N3-G.G
  N20: R20.Pin_1, LP0701N3-G.G, TN2106N3-G.D
  N21: 5V_Input.pin1, F1.1

notes:
  GND
  3.3
  i2c SDA GPIO41
  WindDir GPIO2
  BME280
  i2c SCL GPIO42
  GND,3.3,DO
  -    +
  1wire
  Pin 3+4
  Pin2=3.3V
  Pin4=GND
  Pin1,3,4,6=GND
  Pin7,8=3.3V
  Pin2=SCL
  Rev. 1.3, Jun 2026
  J1+J2 add. 4k7 pullup
  Pin3=WinDir
  Pin5=WindSpd
  Pin5=SDA
  RainSensor
  i2c Pullups for
  longer cabels (BME280)
  1wire (for eg.
  DS18B20)
  Connector for Davis
  Windsensor (Dir+Spd)
  Conntector for BME280
  Connector Davis Rain
  heltec V3
  U1-U6: SMLVT3V3 DO-214AA
  D1-D12: BAT43
  R1-R3: 33 Ω (1/2W)
  R11-R16: 4k7 Ω
  R7-R10: 1k Ω
  R4-R6: 330 Ω (1/2W)
  C4-C10: 100nF cer. 50V
  franzenhof.com
  Rain GPIO7
  WindSpd GPIO6
  (1x BME280 + 3x DS18B20)
  +Rain, i2c, 1Wire
  Heltec V3 / Davis Wind
  ( ADC1_CH1)
  1w GPIO5
  (GPIO6)
  C1-C2: 100uF Elko 25V
  100mA
  for i2c (long distance)
  47 HSS
  R17-R19: 10k Ω
  170mA
  R20: 47k Ω
  C3: 4.7uF ceramic 50V
  900mA
  5v VCC-Input
  (alternative to usb-c)
  D13: STPS3L60QRL (etc.)
  R21: optional 4k7 Ω
  for non Davis-Wind-Dir-Sens
  Leave R21 unpopulated for
  orig. Davis wind-sensors
  C11-C12: 1uF cer. 50V

custom parts:
  MOSFET-PCHANNEL LP0701N3-G: LP0701N3-G
  MOSFET-nCHANNEL VN2222L: VN2222L
